// Logisim project 16BİTLİK_PC.circ as structural Verilog: 30 circuits, main circuit main
module main (
  input  FGO,
  input  FGI,
  input  [7:0] in_3,
  input  Cout,
  output HLT
);

  wire clock_1_out, main_control_1_cle, main_control_1_cme, main_control_1_hlt, main_control_1_outr_load,
       not_1_out;
  wire [1:0] main_control_1_ir_bus_ir_load, main_control_1_m___bus_m___load, main_control_1_tr_bus_tr_load;
  wire [2:0] main_control_1_dr_bus_dr_inc_dr_load;
  wire [3:0] main_control_1_ac_bus_ac_clr_ac_inc_ac_load, main_control_1_ar_bus_ar_inc_ar_clr_ar_load,
       main_control_1_pc_bus_pc_clr_pc_inc_pc_load;
  wire [6:0] main_control_1_alu;
  wire [7:0] n8_bitlik_register_1_output, OUTR_output;
  wire [11:0] AR_output, PC_output;
  wire [14:0] AC_output;
  wire [15:0] controlled_buffer_1_out, DR_output, IR_output, n16_bitlik_alu_1_output, ram_1_data, TR_output;
  wire [15:15] AC_output_2;

  main_control main_control_1 (
    .IR(IR_output), .CLK(HLT), .FGO(FGO), .FGI(FGI), .AC({AC_output_2[15], AC_output}), .E(Cout),
    .AC_15(AC_output_2[15]), .DR(DR_output), .CME(main_control_1_cme), .CLE(main_control_1_cle),
    .HLT(main_control_1_hlt), .M___BUS_M___LOAD(main_control_1_m___bus_m___load),
    .AR_BUS_AR_INC_AR_CLR_AR_LOAD(main_control_1_ar_bus_ar_inc_ar_clr_ar_load),
    .PC_BUS_PC_CLR_PC_INC_PC_LOAD(main_control_1_pc_bus_pc_clr_pc_inc_pc_load),
    .DR_BUS_DR_INC_DR_LOAD(main_control_1_dr_bus_dr_inc_dr_load),
    .AC_BUS_AC_CLR_AC_INC_AC_LOAD(main_control_1_ac_bus_ac_clr_ac_inc_ac_load),
    .OUTR_LOAD(main_control_1_outr_load), .TR_BUS_TR_LOAD(main_control_1_tr_bus_tr_load),
    .IR_BUS_IR_LOAD(main_control_1_ir_bus_ir_load), .ALU(main_control_1_alu));  // open: out_21
  not not_1 (not_1_out, main_control_1_hlt);
  Clock clock_1 (.out(clock_1_out));
  and and_1 (HLT, not_1_out, clock_1_out);
  _8_bitlik_register u_8_bitlik_register_1 (
    .\İNPUT (in_3), .CLK(HLT), .LOAD(1'b1), .OUTPUT(n8_bitlik_register_1_output));
  // Probe on n8_bitlik_register_1_output
  _16_bitlik_alu u_16_bitlik_alu_1 (
    .AC({AC_output_2[15], AC_output}), .DR(DR_output), .INPR(n8_bitlik_register_1_output),
    .AND(main_control_1_alu[0]), .ADD(main_control_1_alu[1]), .CMA(main_control_1_alu[2]),
    .LD_DR(main_control_1_alu[3]), .LD_INPR(main_control_1_alu[4]), .CIR(main_control_1_alu[5]),
    .CIL(main_control_1_alu[6]), .CLA(main_control_1_cle), .CME(main_control_1_cme), .CLOCK(HLT),
    .OUTPUT(n16_bitlik_alu_1_output), .OUTPUT_2(Cout));
  // Probe on n16_bitlik_alu_1_output
  _12_bitlik_register AR (
    .\İNPUT (controlled_buffer_1_out[11:0]), .INC(main_control_1_ar_bus_ar_inc_ar_clr_ar_load[2]), .CLK(HLT),
    .LD(main_control_1_ar_bus_ar_inc_ar_clr_ar_load[0]),
    .CLR(main_control_1_ar_bus_ar_inc_ar_clr_ar_load[1]), .OUTPUT(AR_output));
  // Probe on PC_output
  _12_bitlik_register PC (
    .\İNPUT (controlled_buffer_1_out[11:0]), .INC(main_control_1_pc_bus_pc_clr_pc_inc_pc_load[1]), .CLK(HLT),
    .LD(main_control_1_pc_bus_pc_clr_pc_inc_pc_load[0]),
    .CLR(main_control_1_pc_bus_pc_clr_pc_inc_pc_load[2]), .OUTPUT(PC_output));
  _16_bitlik_register DR (
    .\İNPUT (controlled_buffer_1_out), .CLK(HLT), .INC(main_control_1_dr_bus_dr_inc_dr_load[1]),
    .LD(main_control_1_dr_bus_dr_inc_dr_load[0]), .OUTPUT(DR_output));  // open: CLR
  _16_bitlik_register AC (
    .\İNPUT (n16_bitlik_alu_1_output), .CLK(HLT), .INC(main_control_1_ac_bus_ac_clr_ac_inc_ac_load[1]),
    .CLR(main_control_1_ac_bus_ac_clr_ac_inc_ac_load[2]),
    .LD(main_control_1_ac_bus_ac_clr_ac_inc_ac_load[0]), .OUTPUT({AC_output_2[15], AC_output}));
  // Probe on IR_output
  _16_bitlik_register IR (
    .\İNPUT (controlled_buffer_1_out), .CLK(HLT), .LD(main_control_1_ir_bus_ir_load[0]), .OUTPUT(IR_output));  // open: INC, CLR
  // Probe on TR_output
  _16_bitlik_register TR (
    .\İNPUT (controlled_buffer_1_out), .CLK(HLT), .LD(main_control_1_tr_bus_tr_load[0]), .OUTPUT(TR_output));  // open: INC, CLR
  _8_bitlik_register OUTR (
    .\İNPUT (controlled_buffer_1_out[7:0]), .CLK(HLT), .LOAD(main_control_1_outr_load), .OUTPUT(OUTR_output));
  RAM #(.addrWidth(12), .dataWidth(16), .bus("separate")) ram_1 (
    .addr(AR_output), .din(controlled_buffer_1_out), .data(ram_1_data),
    .str(main_control_1_m___bus_m___load[0]), .clk(HLT));  // open: sel, ld, clr
  // Probe on AR_output
  // Probe on DR_output
  // Probe on {AC_output_2[15], AC_output}
  // Probe on OUTR_output
  assign controlled_buffer_1_out = main_control_1_m___bus_m___load[1] ? ram_1_data : 16'bz;  // Controlled_Buffer controlled_buffer_1
  assign controlled_buffer_1_out = main_control_1_ar_bus_ar_inc_ar_clr_ar_load[3] ? {4'b0000, AR_output} : 16'bz;  // Controlled_Buffer controlled_buffer_2
  assign controlled_buffer_1_out = main_control_1_pc_bus_pc_clr_pc_inc_pc_load[3] ? {4'b0000, PC_output} : 16'bz;  // Controlled_Buffer controlled_buffer_3
  assign controlled_buffer_1_out = main_control_1_dr_bus_dr_inc_dr_load[2] ? DR_output : 16'bz;  // Controlled_Buffer controlled_buffer_4
  assign controlled_buffer_1_out = main_control_1_ac_bus_ac_clr_ac_inc_ac_load[3] ? {AC_output_2[15], AC_output} : 16'bz;  // Controlled_Buffer controlled_buffer_5
  assign controlled_buffer_1_out = main_control_1_ir_bus_ir_load[1] ? IR_output : 16'bz;  // Controlled_Buffer controlled_buffer_6
  assign controlled_buffer_1_out = main_control_1_tr_bus_tr_load[1] ? TR_output : 16'bz;  // Controlled_Buffer controlled_buffer_7
endmodule

module main_control (
  input  E,
  input  [15:0] AC,
  input  [15:0] DR,
  input  AC_15,
  input  [15:0] IR,
  input  CLK,
  input  FGO,
  input  FGI,
  output HLT,
  output [1:0] M___BUS_M___LOAD,
  output [3:0] AR_BUS_AR_INC_AR_CLR_AR_LOAD,
  output [3:0] PC_BUS_PC_CLR_PC_INC_PC_LOAD,
  output [2:0] DR_BUS_DR_INC_DR_LOAD,
  output [3:0] AC_BUS_AC_CLR_AC_INC_AC_LOAD,
  output OUTR_LOAD,
  output [1:0] TR_BUS_TR_LOAD,
  output CME,
  output CLE,
  output [1:0] IR_BUS_IR_LOAD,
  output [6:0] ALU,
  output out_21
);

  wire not_1_out, sc_kontrol_1_sc_clear;
  wire [1:0] decoder_2_out0;
  wire [2:0] flag_kontrol_1_fgi_2;
  wire [3:0] COUNTER_output, decoder_1_out7;
  wire [4:0] decoder_2_out2;
  wire [6:3] decoder_1_out3;

  Decoder #(.select(3)) decoder_1 (
    .out0(decoder_1_out7[3]), .out1(decoder_1_out7[2]), .out2(decoder_1_out7[1]), .out3(decoder_1_out3[3]),
    .out4(decoder_1_out3[4]), .out5(decoder_1_out3[5]), .out6(decoder_1_out3[6]), .out7(decoder_1_out7[0]),
    .sel(IR[14:12]));  // open: en
  SC_kontrol sc_kontrol_1 (
    .D0(decoder_1_out7[3]), .D1(decoder_1_out7[2]), .D2(decoder_1_out7[1]), .D3(decoder_1_out3[3]),
    .D4(decoder_1_out3[4]), .D5(decoder_1_out3[5]), .D6(decoder_1_out3[6]), .D7(decoder_1_out7[0]),
    .T2(decoder_2_out2[0]), .T3(decoder_2_out2[1]), .T4(decoder_2_out2[2]), .T5(decoder_2_out2[3]),
    .T6(decoder_2_out2[4]), .R(flag_kontrol_1_fgi_2[2]), .I(IR[15]), .IR0(IR[0]), .IR1(IR[1]), .IR2(IR[2]),
    .IR3(IR[3]), .IR4(IR[4]), .IR5(IR[5]), .IR6(IR[6]), .IR7(IR[7]), .IR8(IR[8]), .IR9(IR[9]), .IR10(IR[10]),
    .IR11(IR[11]), .SC_CLEAR(sc_kontrol_1_sc_clear));
  counter COUNTER (.CLK(CLK), .SC_CLEAR(sc_kontrol_1_sc_clear), .OUTPUT(COUNTER_output));
  not not_1 (not_1_out, IR[15]);
  Decoder #(.select(4)) decoder_2 (
    .out0(decoder_2_out0[0]), .out1(decoder_2_out0[1]), .out2(decoder_2_out2[0]), .out3(decoder_2_out2[1]),
    .out4(decoder_2_out2[2]), .out5(decoder_2_out2[3]), .out6(decoder_2_out2[4]), .sel(COUNTER_output));  // open: out7, out8, out9, out10, out11, out12, out13, out14, out15, en
  and and_1 (HLT, IR[0], decoder_1_out7[0], not_1_out, decoder_2_out2[1]);
  FLAG_KONTROL flag_kontrol_1 (
    .FGI(FGI), .FGO(FGO), .D7(decoder_1_out7[0]), .I(IR[15]), .T3(decoder_2_out2[1]), .IR7(IR[7]),
    .IR6(IR[6]), .T0(decoder_2_out0[0]), .T1(decoder_2_out0[1]), .T2(decoder_2_out2[0]), .IR10(IR[10]),
    .IR11(IR[11]), .CLOCK(CLK), .IEN(out_21), .FGI_2(flag_kontrol_1_fgi_2[0]),
    .FGO_2(flag_kontrol_1_fgi_2[1]), .R(flag_kontrol_1_fgi_2[2]));
  ALU_kontrol alu_kontrol_1 (
    .D0(decoder_1_out7[3]), .D1(decoder_1_out7[2]), .D2(decoder_1_out7[1]), .D7(decoder_1_out7[0]),
    .I(IR[15]), .T3(decoder_2_out2[1]), .T5(decoder_2_out2[3]), .IR6(IR[6]), .IR7(IR[7]), .IR9(IR[9]),
    .IR11(IR[11]), .AND(ALU[0]), .ADD(ALU[1]), .CMA(ALU[2]), .DR_LOAD(ALU[3]), .INPR_LOAD(ALU[4]),
    .CIR(ALU[5]), .CIL(ALU[6]));
  register_kontrol register_kontrol_1 (
    .R(flag_kontrol_1_fgi_2[2]), .I(IR[15]), .D0(decoder_1_out7[3]), .D1(decoder_1_out7[2]),
    .D2(decoder_1_out7[1]), .D3(decoder_1_out3[3]), .D4(decoder_1_out3[4]), .D5(decoder_1_out3[5]),
    .D6(decoder_1_out3[6]), .D7(decoder_1_out7[0]), .T0(decoder_2_out0[0]), .T1(decoder_2_out0[1]),
    .T2(decoder_2_out2[0]), .T3(decoder_2_out2[1]), .T4(decoder_2_out2[2]), .T5(decoder_2_out2[3]),
    .T6(decoder_2_out2[4]), .IR1(IR[1]), .IR2(IR[2]), .IR3(IR[3]), .IR4(IR[4]), .IR5(IR[5]), .IR6(IR[6]),
    .IR7(IR[7]), .IR8(IR[8]), .IR9(IR[9]), .IR10(IR[10]), .IR11(IR[11]), .FGO(flag_kontrol_1_fgi_2[1]),
    .FGI(flag_kontrol_1_fgi_2[0]), .E(E), .AC(AC), .AC_15(AC_15), .DR(DR), .CME(CME), .CLE(CLE),
    .M___BUS___M___LOAD(M___BUS_M___LOAD), .AR_BUS__AR_INC__AR_CLR___AR_LOAD(AR_BUS_AR_INC_AR_CLR_AR_LOAD),
    .PC_BUS__PC_CLR__PC_INC___PC_LOAD(PC_BUS_PC_CLR_PC_INC_PC_LOAD),
    .DR_BUS__DR_INC___DR_LOAD(DR_BUS_DR_INC_DR_LOAD),
    .AC_BUS__AC_CLR__AC_INC___AC_LOAD(AC_BUS_AC_CLR_AC_INC_AC_LOAD), .OUTR_LOAD(OUTR_LOAD),
    .TR_BUS___TR_LOAD(TR_BUS_TR_LOAD), .IR_BUS___IR_LOAD(IR_BUS_IR_LOAD));

  // Notes on the sheet:
  //   D0..D7
  //   T0..15
endmodule

// REGİSTER KONTROL
module register_kontrol (
  input  FGO,
  input  FGI,
  input  E,
  input  [15:0] AC,
  input  AC_15,
  input  [15:0] DR,
  input  R,
  input  I,
  input  D0,
  input  D1,
  input  D2,
  input  D3,
  input  D4,
  input  D5,
  input  D6,
  input  D7,
  input  T0,
  input  T1,
  input  T2,
  input  T3,
  input  T4,
  input  T5,
  input  T6,
  input  IR1,
  input  IR2,
  input  IR3,
  input  IR4,
  input  IR5,
  input  IR6,
  input  IR7,
  input  IR8,
  input  IR9,
  input  IR10,
  input  IR11,
  output [1:0] M___BUS___M___LOAD,
  output [3:0] AR_BUS__AR_INC__AR_CLR___AR_LOAD,
  output [3:0] PC_BUS__PC_CLR__PC_INC___PC_LOAD,
  output [2:0] DR_BUS__DR_INC___DR_LOAD,
  output [3:0] AC_BUS__AC_CLR__AC_INC___AC_LOAD,
  output OUTR_LOAD,
  output [1:0] TR_BUS___TR_LOAD,
  output [1:0] IR_BUS___IR_LOAD,
  output CME,
  output CLE
);

  OUTR_kontrol OUTR (.D7(D7), .I(I), .T3(T3), .IR10(IR10), .OUTR_LOAD(OUTR_LOAD));
  TR_kontrol TR (.R(R), .T0(T0), .T1(T1), .TR_LOAD(TR_BUS___TR_LOAD[0]), .TR_BUS(TR_BUS___TR_LOAD[1]));
  IR_kontrol IR (.R(R), .T1(T1), .T2(T2), .IR_LOAD(IR_BUS___IR_LOAD[0]), .IR_BUS(IR_BUS___IR_LOAD[1]));
  E_Kontroll u_E (.D7(D7), .I(I), .T3(T3), .B8(IR8), .B10(IR10), .CLE(CLE), .CME(CME));
  AR_kontrol AR (
    .D7(D7), .I(I), .D4(D4), .D5(D5), .R(R), .T0(T0), .T2(T2), .T3(T3), .T4(T4), .T5(T5),
    .AR_LOAD(AR_BUS__AR_INC__AR_CLR___AR_LOAD[0]), .AR_CLEAR(AR_BUS__AR_INC__AR_CLR___AR_LOAD[1]),
    .AR_INC(AR_BUS__AR_INC__AR_CLR___AR_LOAD[2]), .AR_BUS(AR_BUS__AR_INC__AR_CLR___AR_LOAD[3]));
  DR_kontrol u_DR (
    .D0(D0), .D1(D1), .D2(D2), .D6(D6), .T4(T4), .T5(T5), .T6(T6), .DR_LD(DR_BUS__DR_INC___DR_LOAD[0]),
    .DR_INC(DR_BUS__DR_INC___DR_LOAD[1]), .DR_BUS(DR_BUS__DR_INC___DR_LOAD[2]));
  M____kontrol M (
    .R(R), .I(I), .D0(D0), .D1(D1), .D2(D2), .D3(D3), .D5(D5), .D6(D6), .D7(D7), .T1(T1), .T3(T3), .T4(T4),
    .T6(T6), .M___LOAD(M___BUS___M___LOAD[0]), .M___BUS(M___BUS___M___LOAD[1]));
  PC_kontrol PC (
    .DR(DR), .AC_15(AC_15), .AC_15_2(AC_15), .AC(AC), .E(E), .FGI(FGI), .FGO(FGO), .I(I), .R(R), .D4(D4),
    .D5(D5), .D6(D6), .D7(D7), .T0(T0), .T1(T1), .T2(T2), .T3(T3), .T4(T4), .T5(T5), .T6(T6), .IR1(IR1),
    .IR2(IR2), .IR3(IR3), .IR4(IR4), .IR8(IR8), .IR9(IR9), .PC_LD(PC_BUS__PC_CLR__PC_INC___PC_LOAD[0]),
    .PC_INC(PC_BUS__PC_CLR__PC_INC___PC_LOAD[1]), .PC_CLR(PC_BUS__PC_CLR__PC_INC___PC_LOAD[2]),
    .PC_BUS(PC_BUS__PC_CLR__PC_INC___PC_LOAD[3]));
  AC_kontrol u_AC (
    .I(I), .D0(D0), .D1(D1), .D2(D2), .D3(D3), .D4(D4), .D7(D7), .T3(T3), .T4(T4), .T5(T5), .IR5(IR5),
    .IR6(IR6), .IR7(IR7), .IR9(IR9), .IR10(IR10), .IR11(IR11), .AC_LOAD(AC_BUS__AC_CLR__AC_INC___AC_LOAD[0]),
    .AC_INC(AC_BUS__AC_CLR__AC_INC___AC_LOAD[1]), .AC_CLR(AC_BUS__AC_CLR__AC_INC___AC_LOAD[2]),
    .AC_BUS(AC_BUS__AC_CLR__AC_INC___AC_LOAD[3]));
endmodule

module FLAG_KONTROL (
  input  D7,
  input  I,
  input  T3,
  input  IR7,
  input  IR6,
  input  T0,
  input  T1,
  input  T2,
  input  IR10,
  input  IR11,
  input  FGI,
  input  FGO,
  input  CLOCK,
  output IEN,
  output FGI_2,
  output FGO_2,
  output R
);

  IEN_FF u_IEN (.D7(D7), .I(I), .T3(T3), .IR7(IR7), .IR6(IR6), .R(R), .T2(T2), .clock(CLOCK), .IEN(IEN));
  FGI_FF u_FGI (.FGI(FGI), .D7(D7), .I(I), .T3(T3), .IR11(IR11), .CLOCK(CLOCK), .out_7(FGI_2));
  FGO_FF u_FGO (.FGO(FGO), .D7(D7), .I(I), .T3(T3), .IR10(IR10), .CLOCK(CLOCK), .out_7(FGO_2));
  R_kontrol u_R (.IEN(IEN), .FGI(FGI_2), .FGO(FGO_2), .R(R), .T0(T0), .T1(T1), .T2(T2), .clock(CLOCK), .R_2(R));
endmodule

module AR_kontrol (
  input  D7,
  input  I,
  input  D4,
  input  D5,
  input  R,
  input  T0,
  input  T2,
  input  T3,
  input  T4,
  input  T5,
  output AR_LOAD,
  output AR_CLEAR,
  output AR_INC,
  output AR_BUS
);

  wire and_1_out, and_2_out, and_5_out, and_6_out, not_1_out, not_2_out, or_1_out;

  not not_1 (not_1_out, R);
  not not_2 (not_2_out, D7);
  or or_1 (or_1_out, T2, T0);
  and and_1 (and_1_out, or_1_out, not_1_out);
  and and_2 (and_2_out, I, T3, not_2_out);
  and and_3 (AR_CLEAR, R, T0);
  and and_4 (AR_INC, T4, D5);
  and and_5 (and_5_out, T4, D4);
  and and_6 (and_6_out, T5, D5);
  or or_2 (AR_LOAD, and_1_out, and_2_out);
  or or_3 (AR_BUS, and_5_out, and_6_out);
endmodule

module PC_kontrol (
  input  I,
  input  R,
  input  D4,
  input  D5,
  input  D6,
  input  D7,
  input  T0,
  input  T1,
  input  T2,
  input  T3,
  input  T4,
  input  T5,
  input  T6,
  input  IR1,
  input  IR2,
  input  IR3,
  input  IR4,
  input  IR8,
  input  IR9,
  input  [15:0] DR,
  input  AC_15,
  input  AC_15_2,
  input  [15:0] AC,
  input  E,
  input  FGI,
  input  FGO,
  output PC_LD,
  output PC_INC,
  output PC_CLR,
  output PC_BUS
);

  wire and_1_out, and_2_out, and_3_out, and_4_out, and_5_out, and_6_out, and_7_out, and_8_out, and_9_out,
       and_10_out, and_11_out, and_13_out, and_14_out, and_15_out, and_16_out, and_17_out, and_18_out,
       and_19_out, and_20_out, and_21_out, not_1_out, not_2_out, not_3_out, not_4_out, not_5_out, not_6_out,
       not_8_out, not_10_out, or_1_out, p_2_out, p_out, r_2_out, r_3_out, r_4_out, r_out;
  wire [15:0] not_7_out, not_9_out;

  not not_1 (not_1_out, R);
  not not_2 (not_2_out, I);
  not not_3 (not_3_out, I);
  not not_4 (not_4_out, I);
  not not_5 (not_5_out, I);
  and and_1 (and_1_out, not_1_out, T1);
  and and_2 (and_2_out, R, T2);
  and and_3 (and_3_out, T6, D6);
  and u_r (r_out, D7, T3, not_2_out);
  and r_2 (r_2_out, T3, D7, not_3_out);
  and r_3 (r_3_out, T3, not_4_out, D7);
  and r_4 (r_4_out, D7, T3, not_5_out);
  and p (p_out, I, D7, T3);
  and p_2 (p_2_out, T3, D7, I);
  and and_4 (and_4_out, r_out, IR4);
  and and_5 (and_5_out, r_2_out, IR3);
  and and_6 (and_6_out, r_3_out, IR2);
  and and_7 (and_7_out, r_4_out, IR1);
  and and_8 (and_8_out, p_out, IR9);
  and and_9 (and_9_out, p_2_out, IR8);
  not not_6 (not_6_out, R);
  and and_10 (and_10_out, D4, T4);
  and and_11 (and_11_out, T5, D5);
  assign not_7_out = ~DR;  // NOT_Gate not_7, 16 bits wide
  not not_8 (not_8_out, AC_15);
  assign not_9_out = ~AC;  // NOT_Gate not_9, 16 bits wide
  not not_10 (not_10_out, E);
  and and_12 (PC_CLR, T1, R);
  or or_1 (or_1_out, R, not_6_out);
  and and_13 (and_13_out, and_4_out, not_8_out);
  and and_14 (and_14_out, and_5_out, AC_15_2);
  and and_15 (and_15_out, and_7_out, not_10_out);
  and and_16 (and_16_out, and_8_out, FGI);
  and and_17 (and_17_out, T4, D5);
  or or_2 (PC_LD, and_10_out, and_11_out);
  and and_18 (and_18_out, and_9_out, FGO);
  and and_19 (and_19_out, or_1_out, T0);
  or or_3 (PC_BUS, and_19_out, and_17_out);
  and and_20 (and_20_out, and_3_out, not_7_out[0], not_7_out[1], not_7_out[2], not_7_out[3], not_7_out[4], not_7_out[5], not_7_out[6], not_7_out[7], not_7_out[8], not_7_out[9], not_7_out[10], not_7_out[11], not_7_out[12], not_7_out[13], not_7_out[14], not_7_out[15]);
  and and_21 (and_21_out, and_6_out, not_9_out[0], not_9_out[1], not_9_out[2], not_9_out[3], not_9_out[4], not_9_out[5], not_9_out[6], not_9_out[7], not_9_out[8], not_9_out[9], not_9_out[10], not_9_out[11], not_9_out[12], not_9_out[13], not_9_out[14], not_9_out[15]);
  or or_4 (PC_INC, and_1_out, and_2_out, and_20_out, and_13_out, and_14_out, and_21_out, and_15_out, and_16_out, and_18_out);
endmodule

module M____kontrol (
  input  R,
  input  I,
  input  D0,
  input  D1,
  input  D2,
  input  D3,
  input  D5,
  input  D6,
  input  D7,
  input  T1,
  input  T3,
  input  T4,
  input  T6,
  output M___LOAD,
  output M___BUS
);

  wire and_1_out, and_2_out, and_3_out, and_4_out, and_5_out, and_6_out, not_1_out, not_2_out, or_1_out,
       or_2_out;

  or or_1 (or_1_out, D3, D5);
  not not_1 (not_1_out, R);
  not not_2 (not_2_out, D7);
  and and_1 (and_1_out, or_1_out, T4);
  and and_2 (and_2_out, not_2_out, I, T3);
  or or_2 (or_2_out, D0, D1, D2, D6);
  and and_3 (and_3_out, R, T1);
  and and_4 (and_4_out, T6, D6);
  and and_5 (and_5_out, not_1_out, T1);
  and and_6 (and_6_out, or_2_out, T4);
  or or_3 (M___LOAD, and_3_out, and_1_out, and_4_out);
  or or_4 (M___BUS, and_5_out, and_2_out, and_6_out);
endmodule

module DR_kontrol (
  input  D0,
  input  D1,
  input  D2,
  input  D6,
  input  T4,
  input  T5,
  input  T6,
  output DR_LD,
  output DR_INC,
  output DR_BUS
);

  wire or_1_out;

  and and_1 (DR_BUS, T6, D6);
  or or_1 (or_1_out, D0, D1, D2, D6);
  and and_2 (DR_LD, T4, or_1_out);
  and and_3 (DR_INC, T5, D6);
endmodule

module OUTR_kontrol (
  input  D7,
  input  I,
  input  T3,
  input  IR10,
  output OUTR_LOAD
);

  wire and_1_out;

  and and_1 (and_1_out, D7, I, T3);
  and and_2 (OUTR_LOAD, and_1_out, IR10);
endmodule

module IR_kontrol (
  input  R,
  input  T1,
  input  T2,
  output IR_LOAD,
  output IR_BUS
);

  wire not_1_out;

  not not_1 (not_1_out, R);
  and and_1 (IR_LOAD, T1, not_1_out);
  and and_2 (IR_BUS, T2, not_1_out);
endmodule

module TR_kontrol (
  input  R,
  input  T0,
  input  T1,
  output TR_LOAD,
  output TR_BUS
);

  and and_1 (TR_LOAD, T0, R);
  and and_2 (TR_BUS, T1, R);
endmodule

module AC_kontrol (
  input  I,
  input  D0,
  input  D1,
  input  D2,
  input  D3,
  input  D4,
  input  D7,
  input  T3,
  input  T4,
  input  T5,
  input  IR5,
  input  IR6,
  input  IR7,
  input  IR9,
  input  IR10,
  input  IR11,
  output AC_LOAD,
  output AC_INC,
  output AC_CLR,
  output AC_BUS
);

  wire and_1_out, and_4_out, and_5_out, and_6_out, not_1_out, not_2_out, not_3_out, or_1_out, or_2_out,
       p_out, r_out;

  or or_1 (or_1_out, D0, D1, D2);
  not not_1 (not_1_out, I);
  not not_2 (not_2_out, I);
  not not_3 (not_3_out, I);
  and and_1 (and_1_out, T5, or_1_out);
  and r (r_out, T3, D7, not_1_out);
  or or_2 (or_2_out, IR9, IR7, IR6);
  and p (p_out, IR11, I, D7, T3);
  and and_2 (AC_INC, IR5, T3, D7, not_2_out);
  and and_3 (AC_CLR, T3, IR11, D7, not_3_out);
  and and_4 (and_4_out, D3, T4);
  and and_5 (and_5_out, D7, I, T3, IR10);
  and and_6 (and_6_out, r_out, or_2_out);
  or or_3 (AC_BUS, and_4_out, and_5_out);
  or or_4 (AC_LOAD, and_1_out, and_6_out, p_out);
endmodule

// SC_CLEAR
module SC_kontrol (
  input  D0,
  input  D1,
  input  D2,
  input  D3,
  input  D4,
  input  D5,
  input  D6,
  input  D7,
  input  T2,
  input  T3,
  input  T4,
  input  T5,
  input  T6,
  input  R,
  input  I,
  input  IR0,
  input  IR1,
  input  IR2,
  input  IR3,
  input  IR4,
  input  IR5,
  input  IR6,
  input  IR7,
  input  IR8,
  input  IR9,
  input  IR10,
  input  IR11,
  output SC_CLEAR
);

  wire and_1_out, and_2_out, and_3_out, and_4_out, and_5_out, and_6_out, and_7_out, and_8_out, and_9_out,
       not_1_out, or_1_out, or_2_out, or_3_out, or_4_out, or_5_out;

  and and_1 (and_1_out, T2, R);
  or or_1 (or_1_out, D3, D4);
  or or_2 (or_2_out, D0, D1, D2, D5);
  or or_3 (or_3_out, IR6, IR7, IR8, IR9, IR10, IR11);
  and and_2 (and_2_out, I, D7);
  not not_1 (not_1_out, I);
  and and_3 (and_3_out, not_1_out, D7);
  or or_4 (or_4_out, IR0, IR1, IR2, IR3, IR4, IR5, IR6, IR7, IR8, IR9, IR10, IR11);
  and and_4 (and_4_out, and_3_out, or_4_out);
  and and_5 (and_5_out, or_3_out, and_2_out);
  and and_6 (and_6_out, T5, or_2_out);
  and and_7 (and_7_out, T4, or_1_out);
  and and_8 (and_8_out, T6, D6);
  or or_5 (or_5_out, and_5_out, and_4_out);
  and and_9 (and_9_out, or_5_out, T3);
  or or_6 (SC_CLEAR, and_9_out, and_1_out, and_6_out, and_7_out, and_8_out);
endmodule

// ALU_KONTROL
module ALU_kontrol (
  input  D0,
  input  D1,
  input  D2,
  input  D7,
  input  I,
  input  T3,
  input  T5,
  input  IR6,
  input  IR7,
  input  IR9,
  input  IR11,
  output AND,
  output ADD,
  output CMA,
  output DR_LOAD,
  output INPR_LOAD,
  output CIR,
  output CIL
);

  wire and_1_out, and_2_out, not_1_out;

  not not_1 (not_1_out, I);
  and and_1 (and_1_out, T3, not_1_out, D7);
  and and_2 (and_2_out, D7, I, T3);
  and and_3 (AND, D0, T5);
  and and_4 (ADD, D1, T5);
  and and_5 (CMA, and_1_out, IR9);
  and and_6 (DR_LOAD, D2, T5);
  and and_7 (INPR_LOAD, and_2_out, IR11);
  and and_8 (CIR, and_1_out, IR7);
  and and_9 (CIL, and_1_out, IR6);
endmodule

module R_kontrol (
  input  R,
  input  T0,
  input  T1,
  input  T2,
  input  IEN,
  input  FGI,
  input  FGO,
  input  clock,
  output R_2
);

  wire and_1_out, and_2_out, not_1_out, not_2_out, not_3_out, or_1_out;

  not not_1 (not_1_out, T2);
  not not_2 (not_2_out, T1);
  not not_3 (not_3_out, T0);
  or or_1 (or_1_out, FGI, FGO);
  and and_1 (and_1_out, R, T2);
  and and_2 (and_2_out, not_1_out, not_2_out, not_3_out, IEN, or_1_out);
  J_K_Flip_Flop j_k_ff_1 (.J(and_2_out), .clk(clock), .K(and_1_out), .Q(R_2));  // open: Qn, preset, en, reset
endmodule

module E_Kontroll (
  input  D7,
  input  I,
  input  T3,
  input  B8,
  input  B10,
  output CLE,
  output CME
);

  wire not_1_out, R_out;

  not not_1 (not_1_out, I);
  and R (R_out, D7, not_1_out, T3);
  and and_1 (CLE, R_out, B10);
  and and_2 (CME, R_out, B8);
endmodule

module FGO_FF (
  input  D7,
  input  I,
  input  T3,
  input  IR10,
  input  CLOCK,
  input  FGO,
  output out_7
);

  wire and_1_out, and_2_out, and_3_out, and_4_out, and_5_out, and_6_out, or_1_out, or_2_out;

  and and_1 (and_1_out, ~and_2_out, FGO);  // AND_Gate
  and and_2 (and_2_out, IR10, T3, I, D7);
  and and_3 (and_3_out, and_1_out, 1'b1);
  and and_4 (and_4_out, and_1_out, ~1'b1);  // AND_Gate
  and and_5 (and_5_out, and_2_out, ~1'b1);  // AND_Gate
  and and_6 (and_6_out, and_2_out, 1'b1);
  or or_1 (or_1_out, and_3_out, and_5_out);
  or or_2 (or_2_out, and_4_out, and_6_out);
  J_K_Flip_Flop j_k_ff_1 (.J(or_1_out), .clk(CLOCK), .K(or_2_out), .Q(out_7));  // open: Qn, preset, en, reset
endmodule

module FGI_FF (
  input  D7,
  input  I,
  input  T3,
  input  IR11,
  input  CLOCK,
  input  FGI,
  output out_7
);

  wire and_1_out, and_2_out, and_3_out, and_4_out, and_5_out, and_6_out, or_1_out, or_2_out;

  and and_1 (and_1_out, ~and_2_out, FGI);  // AND_Gate
  and and_2 (and_2_out, IR11, T3, I, D7);
  and and_3 (and_3_out, and_1_out, 1'b1);
  and and_4 (and_4_out, and_1_out, ~1'b1);  // AND_Gate
  and and_5 (and_5_out, and_2_out, ~1'b1);  // AND_Gate
  and and_6 (and_6_out, and_2_out, 1'b1);
  or or_1 (or_1_out, and_3_out, and_5_out);
  or or_2 (or_2_out, and_4_out, and_6_out);
  J_K_Flip_Flop j_k_ff_1 (.J(or_1_out), .clk(CLOCK), .K(or_2_out), .Q(out_7));  // open: Qn, preset, en, reset
endmodule

module IEN_FF (
  input  D7,
  input  I,
  input  T3,
  input  IR7,
  input  IR6,
  input  R,
  input  T2,
  input  clock,
  output IEN
);

  wire and_1_out, and_2_out, and_3_out, or_1_out, P_out;

  and P (P_out, D7, I, T3);
  and and_1 (and_1_out, IR7, P_out);
  and and_2 (and_2_out, P_out, IR6);
  or or_1 (or_1_out, and_2_out, and_3_out);
  and and_3 (and_3_out, R, T2);
  J_K_Flip_Flop j_k_ff_1 (.J(and_1_out), .clk(clock), .K(or_1_out), .Q(IEN));  // open: Qn, preset, en, reset
endmodule

// reg
module _4_Bitlik_register (
  input  INC,
  input  LD,
  input  [3:0] \İNPUT ,
  input  CLR,
  input  CLK,
  output [3:0] OUTPUT,
  output elde
);

  wire and_1_out, and_2_out, and_3_out, and_4_out, and_5_out, and_6_out, and_7_out, and_8_out, and_9_out,
       and_10_out, and_11_out, and_12_out, not_1_out, not_2_out, not_3_out, not_4_out, not_5_out, not_6_out,
       or_1_out, or_2_out, or_3_out, or_4_out, or_5_out, or_6_out, or_7_out, or_8_out;

  not not_1 (not_1_out, LD);
  not not_2 (not_2_out, not_1_out);
  and and_1 (and_1_out, INC, not_1_out);
  not not_3 (not_3_out, \İNPUT [0]);
  not not_4 (not_4_out, \İNPUT [1]);
  not not_5 (not_5_out, \İNPUT [2]);
  not not_6 (not_6_out, \İNPUT [3]);
  and and_2 (and_2_out, not_2_out, \İNPUT [0]);
  and and_3 (and_3_out, not_2_out, not_3_out);
  and and_4 (and_4_out, not_2_out, \İNPUT [1]);
  and and_5 (and_5_out, not_2_out, not_4_out);
  and and_6 (and_6_out, not_2_out, \İNPUT [2]);
  and and_7 (and_7_out, not_2_out, not_5_out);
  and and_8 (and_8_out, not_2_out, \İNPUT [3]);
  and and_9 (and_9_out, not_2_out, not_6_out);
  and and_10 (and_10_out, and_1_out, OUTPUT[0]);
  and and_11 (and_11_out, and_1_out, OUTPUT[0], OUTPUT[1]);
  or or_1 (or_1_out, and_1_out, and_2_out);
  or or_2 (or_2_out, and_1_out, and_3_out);
  or or_3 (or_3_out, and_4_out, and_10_out);
  or or_4 (or_4_out, and_10_out, and_5_out);
  or or_5 (or_5_out, and_6_out, and_11_out);
  or or_6 (or_6_out, and_11_out, and_7_out);
  and and_12 (and_12_out, OUTPUT[2], OUTPUT[1], OUTPUT[0], and_1_out);
  or or_7 (or_7_out, and_8_out, and_12_out);
  or or_8 (or_8_out, and_12_out, and_9_out);
  J_K_Flip_Flop j_k_ff_1 (.J(or_1_out), .clk(CLK), .K(or_2_out), .Q(OUTPUT[0]), .reset(CLR));  // open: Qn, preset, en
  J_K_Flip_Flop j_k_ff_2 (.J(or_3_out), .clk(CLK), .K(or_4_out), .Q(OUTPUT[1]), .reset(CLR));  // open: Qn, preset, en
  J_K_Flip_Flop j_k_ff_3 (.J(or_5_out), .clk(CLK), .K(or_6_out), .Q(OUTPUT[2]), .reset(CLR));  // open: Qn, preset, en
  J_K_Flip_Flop j_k_ff_4 (.J(or_7_out), .clk(CLK), .K(or_8_out), .Q(OUTPUT[3]), .reset(CLR));  // open: Qn, preset, en
  and and_13 (elde, OUTPUT[0], OUTPUT[1], OUTPUT[3], OUTPUT[2]);
endmodule

module _8_bitlik_register (
  input  [7:0] \İNPUT ,
  input  CLK,
  input  LOAD,
  output [7:0] OUTPUT
);

  _4_Bitlik_register u_4_bitlik_register_1 (
    .CLK(CLK), .\İNPUT (\İNPUT [3:0]), .LD(LOAD), .OUTPUT(OUTPUT[3:0]));  // open: elde, INC, CLR
  _4_Bitlik_register u_4_bitlik_register_2 (
    .CLK(CLK), .\İNPUT (\İNPUT [7:4]), .LD(LOAD), .OUTPUT(OUTPUT[7:4]));  // open: elde, INC, CLR
endmodule

module _12_bitlik_register (
  input  [11:0] \İNPUT ,
  input  LD,
  input  CLK,
  input  INC,
  input  CLR,
  output [11:0] OUTPUT
);

  wire and_1_out, and_2_out, n4_bitlik_register_1_elde, n4_bitlik_register_2_elde;

  _4_Bitlik_register u_4_bitlik_register_1 (
    .CLK(CLK), .elde(n4_bitlik_register_1_elde), .\İNPUT (\İNPUT [3:0]), .INC(INC), .LD(LD), .CLR(CLR),
    .OUTPUT(OUTPUT[3:0]));
  _4_Bitlik_register u_4_bitlik_register_2 (
    .CLK(CLK), .elde(n4_bitlik_register_2_elde), .\İNPUT (\İNPUT [7:4]), .INC(and_1_out), .LD(LD), .CLR(CLR),
    .OUTPUT(OUTPUT[7:4]));
  and and_1 (and_1_out, INC, n4_bitlik_register_1_elde);
  _4_Bitlik_register u_4_bitlik_register_3 (
    .CLK(CLK), .\İNPUT (\İNPUT [11:8]), .INC(and_2_out), .LD(LD), .CLR(CLR), .OUTPUT(OUTPUT[11:8]));  // open: elde
  and and_2 (and_2_out, INC, n4_bitlik_register_2_elde);
endmodule

module _16_bitlik_register (
  input  [15:0] \İNPUT ,
  input  INC,
  input  CLK,
  input  LD,
  input  CLR,
  output [15:0] OUTPUT
);

  _4_Bitlik_register u_4_bitlik_register_1 (
    .CLK(CLK), .\İNPUT (\İNPUT [3:0]), .INC(INC), .LD(LD), .CLR(CLR), .OUTPUT(OUTPUT[3:0]));  // open: elde
  _4_Bitlik_register u_4_bitlik_register_2 (
    .CLK(CLK), .\İNPUT (\İNPUT [7:4]), .INC(INC), .LD(LD), .CLR(CLR), .OUTPUT(OUTPUT[7:4]));  // open: elde
  _4_Bitlik_register u_4_bitlik_register_3 (
    .CLK(CLK), .\İNPUT (\İNPUT [11:8]), .LD(LD), .CLR(CLR), .OUTPUT(OUTPUT[11:8]));  // open: elde, INC
  _4_Bitlik_register u_4_bitlik_register_4 (
    .CLK(CLK), .\İNPUT (\İNPUT [15:12]), .INC(INC), .LD(LD), .CLR(CLR), .OUTPUT(OUTPUT[15:12]));  // open: elde
endmodule

module ALU_1_bit (
  input  INPR,
  input  DR,
  input  AC,
  input  AND,
  input  Cin,
  input  ADD,
  input  CMA,
  input  LD_DR,
  input  LD_INPR,
  input  CIR,
  input  \AC_İ_1 ,
  input  CIL,
  input  \AC_İ_1_2 ,
  output Cout,
  output AC_OUTPUT
);

  wire adder_1_out, AND_2_out, AND_out, CMA_out, LD_DR_out, LD_INPR_out, not_1_out, SHL_out, SHR_out;

  Adder #(.width(1)) adder_1 (.a(AC), .b(DR), .out(adder_1_out), .cin(Cin), .cout(Cout));
  not not_1 (not_1_out, AC);
  and u_AND (AND_out, AND, AC, DR);
  and AND_2 (AND_2_out, ADD, adder_1_out);
  and u_CMA (CMA_out, CMA, not_1_out);
  and u_LD_DR (LD_DR_out, LD_DR, DR);
  and u_LD_INPR (LD_INPR_out, LD_INPR, INPR);
  and SHR (SHR_out, CIR, \AC_İ_1 );
  and SHL (SHL_out, CIL, \AC_İ_1_2 );
  or or_1 (AC_OUTPUT, AND_out, AND_2_out, CMA_out, LD_DR_out, LD_INPR_out, SHR_out, SHL_out);
endmodule

// ALU
module _16_bitlik_alu (
  input  [15:0] AC,
  input  [15:0] DR,
  input  [7:0] INPR,
  input  AND,
  input  ADD,
  input  CMA,
  input  LD_DR,
  input  LD_INPR,
  input  CIR,
  input  CIL,
  input  CLA,
  input  CME,
  input  CLOCK,
  output [15:0] OUTPUT,
  output OUTPUT_2
);

  wire alu_1_bit_1_cout, alu_1_bit_2_cout, alu_1_bit_3_cout, alu_1_bit_4_cout, alu_1_bit_5_cout,
       alu_1_bit_6_cout, alu_1_bit_7_cout, alu_1_bit_8_cout, alu_1_bit_9_cout, alu_1_bit_10_cout,
       alu_1_bit_11_cout, alu_1_bit_12_cout, alu_1_bit_13_cout, alu_1_bit_14_cout, alu_1_bit_15_cout,
       alu_1_bit_16_cout, elde_1_cin, \elde_1_i̇_1 , \elde_1_i̇_1_2 ;

  // Probe on AC
  // Probe on DR
  // Probe on INPR
  ALU_1_bit alu_1_bit_1 (
    .AND(AND), .ADD(ADD), .CMA(CMA), .LD_DR(LD_DR), .LD_INPR(LD_INPR), .CIR(CIR), .CIL(CIL), .INPR(INPR[0]),
    .DR(DR[0]), .AC(AC[0]), .Cin(elde_1_cin), .Cout(alu_1_bit_1_cout), .\AC_İ_1 (AC[1]),
    .\AC_İ_1_2 (\elde_1_i̇_1 ), .AC_OUTPUT(OUTPUT[0]));
  ALU_1_bit alu_1_bit_2 (
    .AND(AND), .ADD(ADD), .CMA(CMA), .LD_DR(LD_DR), .LD_INPR(LD_INPR), .CIR(CIR), .CIL(CIL), .INPR(INPR[1]),
    .DR(DR[1]), .AC(AC[1]), .Cin(alu_1_bit_1_cout), .Cout(alu_1_bit_2_cout), .\AC_İ_1 (AC[2]),
    .\AC_İ_1_2 (AC[0]), .AC_OUTPUT(OUTPUT[1]));
  ALU_1_bit alu_1_bit_3 (
    .AND(AND), .ADD(ADD), .CMA(CMA), .LD_DR(LD_DR), .LD_INPR(LD_INPR), .CIR(CIR), .CIL(CIL), .INPR(INPR[2]),
    .DR(DR[2]), .AC(AC[2]), .Cin(alu_1_bit_2_cout), .Cout(alu_1_bit_3_cout), .\AC_İ_1 (AC[3]),
    .\AC_İ_1_2 (AC[1]), .AC_OUTPUT(OUTPUT[2]));
  ALU_1_bit alu_1_bit_4 (
    .AND(AND), .ADD(ADD), .CMA(CMA), .LD_DR(LD_DR), .LD_INPR(LD_INPR), .CIR(CIR), .CIL(CIL), .INPR(INPR[3]),
    .DR(DR[3]), .AC(AC[3]), .Cin(alu_1_bit_3_cout), .Cout(alu_1_bit_4_cout), .\AC_İ_1 (AC[4]),
    .\AC_İ_1_2 (AC[2]), .AC_OUTPUT(OUTPUT[3]));
  ALU_1_bit alu_1_bit_5 (
    .AND(AND), .ADD(ADD), .CMA(CMA), .LD_DR(LD_DR), .LD_INPR(LD_INPR), .CIR(CIR), .CIL(CIL), .INPR(INPR[4]),
    .DR(DR[4]), .AC(AC[4]), .Cin(alu_1_bit_4_cout), .Cout(alu_1_bit_5_cout), .\AC_İ_1 (AC[5]),
    .\AC_İ_1_2 (AC[3]), .AC_OUTPUT(OUTPUT[4]));
  ALU_1_bit alu_1_bit_6 (
    .AND(AND), .ADD(ADD), .CMA(CMA), .LD_DR(LD_DR), .LD_INPR(LD_INPR), .CIR(CIR), .CIL(CIL), .INPR(INPR[5]),
    .DR(DR[5]), .AC(AC[5]), .Cin(alu_1_bit_5_cout), .Cout(alu_1_bit_6_cout), .\AC_İ_1 (AC[6]),
    .\AC_İ_1_2 (AC[4]), .AC_OUTPUT(OUTPUT[5]));
  ALU_1_bit alu_1_bit_7 (
    .AND(AND), .ADD(ADD), .CMA(CMA), .LD_DR(LD_DR), .LD_INPR(LD_INPR), .CIR(CIR), .CIL(CIL), .INPR(INPR[6]),
    .DR(DR[6]), .AC(AC[6]), .Cin(alu_1_bit_6_cout), .Cout(alu_1_bit_7_cout), .\AC_İ_1 (AC[7]),
    .\AC_İ_1_2 (AC[5]), .AC_OUTPUT(OUTPUT[6]));
  ALU_1_bit alu_1_bit_8 (
    .AND(AND), .ADD(ADD), .CMA(CMA), .LD_DR(LD_DR), .LD_INPR(LD_INPR), .CIR(CIR), .CIL(CIL), .INPR(INPR[7]),
    .DR(DR[7]), .AC(AC[7]), .Cin(alu_1_bit_7_cout), .Cout(alu_1_bit_8_cout), .\AC_İ_1 (AC[8]),
    .\AC_İ_1_2 (AC[6]), .AC_OUTPUT(OUTPUT[7]));
  ALU_1_bit alu_1_bit_9 (
    .AND(AND), .ADD(ADD), .CMA(CMA), .LD_DR(LD_DR), .LD_INPR(LD_INPR), .CIR(CIR), .CIL(CIL), .INPR(1'b0),
    .DR(DR[8]), .AC(AC[8]), .Cin(alu_1_bit_8_cout), .Cout(alu_1_bit_9_cout), .\AC_İ_1 (AC[9]),
    .\AC_İ_1_2 (AC[7]), .AC_OUTPUT(OUTPUT[8]));
  ALU_1_bit alu_1_bit_10 (
    .AND(AND), .ADD(ADD), .CMA(CMA), .LD_DR(LD_DR), .LD_INPR(LD_INPR), .CIR(CIR), .CIL(CIL), .INPR(1'b0),
    .DR(DR[9]), .AC(AC[9]), .Cin(alu_1_bit_9_cout), .Cout(alu_1_bit_10_cout), .\AC_İ_1 (AC[10]),
    .\AC_İ_1_2 (AC[8]), .AC_OUTPUT(OUTPUT[9]));
  ALU_1_bit alu_1_bit_11 (
    .AND(AND), .ADD(ADD), .CMA(CMA), .LD_DR(LD_DR), .LD_INPR(LD_INPR), .CIR(CIR), .CIL(CIL), .INPR(1'b0),
    .DR(DR[10]), .AC(AC[10]), .Cin(alu_1_bit_10_cout), .Cout(alu_1_bit_11_cout), .\AC_İ_1 (AC[11]),
    .\AC_İ_1_2 (AC[9]), .AC_OUTPUT(OUTPUT[10]));
  ALU_1_bit alu_1_bit_12 (
    .AND(AND), .ADD(ADD), .CMA(CMA), .LD_DR(LD_DR), .LD_INPR(LD_INPR), .CIR(CIR), .CIL(CIL), .INPR(1'b0),
    .DR(DR[11]), .AC(AC[11]), .Cin(alu_1_bit_11_cout), .Cout(alu_1_bit_12_cout), .\AC_İ_1 (AC[12]),
    .\AC_İ_1_2 (AC[10]), .AC_OUTPUT(OUTPUT[11]));
  ALU_1_bit alu_1_bit_13 (
    .AND(AND), .ADD(ADD), .CMA(CMA), .LD_DR(LD_DR), .LD_INPR(LD_INPR), .CIR(CIR), .CIL(CIL), .INPR(1'b0),
    .DR(DR[12]), .AC(AC[12]), .Cin(alu_1_bit_12_cout), .Cout(alu_1_bit_13_cout), .\AC_İ_1 (AC[13]),
    .\AC_İ_1_2 (AC[11]), .AC_OUTPUT(OUTPUT[12]));
  ALU_1_bit alu_1_bit_14 (
    .AND(AND), .ADD(ADD), .CMA(CMA), .LD_DR(LD_DR), .LD_INPR(LD_INPR), .CIR(CIR), .CIL(CIL), .INPR(1'b0),
    .DR(DR[13]), .AC(AC[13]), .Cin(alu_1_bit_13_cout), .Cout(alu_1_bit_14_cout), .\AC_İ_1 (AC[14]),
    .\AC_İ_1_2 (AC[12]), .AC_OUTPUT(OUTPUT[13]));
  ALU_1_bit alu_1_bit_15 (
    .AND(AND), .ADD(ADD), .CMA(CMA), .LD_DR(LD_DR), .LD_INPR(LD_INPR), .CIR(CIR), .CIL(CIL), .INPR(1'b0),
    .DR(DR[14]), .AC(AC[14]), .Cin(alu_1_bit_14_cout), .Cout(alu_1_bit_15_cout), .\AC_İ_1 (AC[15]),
    .\AC_İ_1_2 (AC[13]), .AC_OUTPUT(OUTPUT[14]));
  ALU_1_bit alu_1_bit_16 (
    .AND(AND), .ADD(ADD), .CMA(CMA), .LD_DR(LD_DR), .LD_INPR(LD_INPR), .CIR(CIR), .CIL(CIL), .INPR(1'b0),
    .DR(DR[15]), .AC(AC[15]), .Cin(alu_1_bit_15_cout), .Cout(alu_1_bit_16_cout), .\AC_İ_1 (\elde_1_i̇_1_2 ),
    .\AC_İ_1_2 (AC[14]), .AC_OUTPUT(OUTPUT[15]));
  // Probe on OUTPUT
  ELDE elde_1 (
    .Cout(alu_1_bit_16_cout), .ADD(ADD), .AC_0(\elde_1_i̇_1 ), .CIR(CIR), .AC_15(\elde_1_i̇_1_2 ), .CIL(CIL),
    .CME(CME), .CLK(CLOCK), .CLE(CLA), .OUTPUT(OUTPUT_2), .\İ_1 (\elde_1_i̇_1 ), .\İ_1_2 (\elde_1_i̇_1_2 ),
    .Cin(elde_1_cin));
endmodule

module counter (
  input  CLK,
  input  SC_CLEAR,
  output [3:0] OUTPUT
);

  wire and_1_out, register_1_q;

  Counter #(.width(4), .max('hf)) counter_1 (
    .count(1'b1), .Q(OUTPUT), .clk(CLK), .clr(register_1_q));  // open: load, D, carry
  Register #(.width(1)) register_1 (.D(SC_CLEAR), .Q(register_1_q), .clk(CLK), .clr(and_1_out));  // open: en
  and and_1 (and_1_out, CLK, SC_CLEAR);
endmodule

module PC_KONTROL_BUF (
  input  I,
  input  R,
  input  D4,
  input  D5,
  input  D6,
  input  D7,
  input  T0,
  input  T1,
  input  T2,
  input  T3,
  input  T4,
  input  T5,
  input  T6,
  input  IR1,
  input  IR2,
  input  IR3,
  input  IR4,
  input  IR8,
  input  IR9,
  input  DR,
  input  AC_15,
  input  AC_15_2,
  input  AC,
  input  E,
  input  FGI,
  input  FGO,
  output PC_LD,
  output PC_INC,
  output PC_CLR,
  output PC_BUS
);

  wire and_1_out, and_2_out, and_3_out, and_4_out, and_5_out, and_6_out, and_7_out, and_8_out, and_9_out,
       and_11_out, and_12_out, and_13_out, and_14_out, controlled_buffer_1_out, controlled_buffer_2_out,
       controlled_buffer_3_out, controlled_buffer_4_out, controlled_buffer_5_out, controlled_buffer_6_out,
       controlled_buffer_7_out, not_1_out, not_2_out, not_3_out, not_4_out, not_5_out, not_6_out, not_7_out,
       not_8_out, not_9_out, not_10_out, or_1_out, p_2_out, p_out, r_2_out, r_3_out, r_4_out, r_out;

  not not_1 (not_1_out, R);
  not not_2 (not_2_out, I);
  not not_3 (not_3_out, I);
  not not_4 (not_4_out, I);
  not not_5 (not_5_out, I);
  and and_1 (and_1_out, not_1_out, T1);
  and and_2 (and_2_out, R, T2);
  and and_3 (and_3_out, T6, D6);
  and u_r (r_out, D7, T3, not_2_out);
  and r_2 (r_2_out, T3, D7, not_3_out);
  and r_3 (r_3_out, T3, not_4_out, D7);
  and r_4 (r_4_out, D7, T3, not_5_out);
  and p (p_out, I, D7, T3);
  and p_2 (p_2_out, T3, D7, I);
  assign controlled_buffer_1_out = not_6_out ? and_3_out : 1'bz;  // Controlled_Buffer controlled_buffer_1
  not not_6 (not_6_out, DR);
  and and_4 (and_4_out, r_out, IR4);
  and and_5 (and_5_out, r_2_out, IR3);
  and and_6 (and_6_out, r_3_out, IR2);
  and and_7 (and_7_out, r_4_out, IR1);
  and and_8 (and_8_out, p_out, IR9);
  and and_9 (and_9_out, p_2_out, IR8);
  and and_10 (PC_CLR, T1, R);
  or or_1 (or_1_out, R, not_7_out);
  not not_7 (not_7_out, R);
  and and_11 (and_11_out, D4, T4);
  and and_12 (and_12_out, T5, D5);
  assign controlled_buffer_2_out = not_8_out ? and_4_out : 1'bz;  // Controlled_Buffer controlled_buffer_2
  not not_8 (not_8_out, AC_15);
  assign controlled_buffer_3_out = AC_15_2 ? and_5_out : 1'bz;  // Controlled_Buffer controlled_buffer_3
  assign controlled_buffer_4_out = not_9_out ? and_6_out : 1'bz;  // Controlled_Buffer controlled_buffer_4
  not not_9 (not_9_out, AC);
  assign controlled_buffer_5_out = not_10_out ? and_7_out : 1'bz;  // Controlled_Buffer controlled_buffer_5
  not not_10 (not_10_out, E);
  assign controlled_buffer_6_out = FGI ? and_8_out : 1'bz;  // Controlled_Buffer controlled_buffer_6
  assign controlled_buffer_7_out = FGO ? and_9_out : 1'bz;  // Controlled_Buffer controlled_buffer_7
  and and_13 (and_13_out, or_1_out, T0);
  and and_14 (and_14_out, T4, D5);
  or or_2 (PC_LD, and_11_out, and_12_out);
  or or_3 (PC_BUS, and_13_out, and_14_out);
  or or_4 (PC_INC, and_1_out, and_2_out, controlled_buffer_1_out, controlled_buffer_2_out, controlled_buffer_3_out, controlled_buffer_4_out, controlled_buffer_5_out, controlled_buffer_6_out, controlled_buffer_7_out);
endmodule

module S_kontrol (
  input  D7,
  input  I,
  input  T3,
  input  IR0,
  output S_CLR
);

  wire not_1_out;

  not not_1 (not_1_out, I);
  and and_1 (S_CLR, IR0, T3, not_1_out, D7);
endmodule

module I_kontrol (
  input  R,
  input  T2,
  input  in_3,
  output out_4
);

  wire and_1_out, not_1_out;

  not not_1 (not_1_out, R);
  and and_1 (and_1_out, not_1_out, T2);
  T_Flip_Flop t_ff_1 (.clk(in_3), .T(and_1_out), .Q(out_4));  // open: Qn, preset, reset, en
endmodule

module ELDE (
  input  Cout,
  input  ADD,
  input  AC_0,
  input  CIR,
  input  AC_15,
  input  CIL,
  input  CME,
  input  CLK,
  input  CLE,
  output OUTPUT,
  output \İ_1 ,
  output \İ_1_2 ,
  output Cin
);

  wire and_1_out, and_2_out, and_3_out, and_4_out, and_5_out, and_6_out, and_7_out, and_8_out, and_9_out,
       and_10_out, and_11_out, not_1_out, or_1_out, or_2_out, or_3_out, or_4_out, or_5_out, or_6_out,
       or_7_out, \ÖNCEKİ_DRUUM_q ;

  and and_1 (and_1_out, Cout, ADD);
  and and_2 (and_2_out, AC_0, CIR);
  or or_1 (or_1_out, and_1_out, and_2_out, and_3_out);
  and and_3 (and_3_out, AC_15, CIL);
  or or_2 (or_2_out, Cout, AC_0, AC_15);
  and and_4 (and_4_out, ~AC_15, ~AC_0, ~Cout);  // AND_Gate
  and and_5 (and_5_out, and_4_out, or_3_out);
  or or_3 (or_3_out, CIL, CIR, ADD);
  not not_1 (not_1_out, or_1_out);
  and and_6 (and_6_out, or_1_out, or_2_out);
  and and_7 (and_7_out, or_2_out, not_1_out);
  and and_8 (and_8_out, ~and_5_out, and_6_out);  // AND_Gate
  and and_9 (and_9_out, ~and_5_out, and_7_out);  // AND_Gate
  and and_10 (and_10_out, 1'b0, and_5_out);
  and and_11 (and_11_out, 1'b1, and_5_out);
  or or_4 (or_4_out, and_8_out, and_10_out);
  or or_5 (or_5_out, and_9_out, and_11_out);
  or or_6 (or_6_out, or_4_out, CME);
  or or_7 (or_7_out, or_5_out, CME);
  J_K_Flip_Flop \YENİ_DURUM  (.J(or_6_out), .clk(CLK), .K(or_7_out), .Q(OUTPUT), .reset(CLE));  // open: Qn, preset, en
  D_Flip_Flop \u_ÖNCEKİ_DRUUM  (.clk(CLK), .D(OUTPUT), .Q(\ÖNCEKİ_DRUUM_q ), .reset(CLE));  // open: Qn, preset, en
  and and_12 (\İ_1 , \ÖNCEKİ_DRUUM_q , and_3_out);
  and and_13 (\İ_1_2 , \ÖNCEKİ_DRUUM_q , and_2_out);
  and and_14 (Cin, \ÖNCEKİ_DRUUM_q , and_1_out);
endmodule
